# Fritzing sketch Zigbee RFID (saved by Fritzing 1.0.2b)
breadboards: 1

parts:
  PN532 = PN532 Elechouse RFID NFC Module V3
  Buzzer = Piezo Speaker
  Arduino = Arduino Nano Every
  Zigbee_Left = Zigbee-PA-Left [form="♀ (female)" package=THT]
  Zigbee_Right = Zigbee-PA-Right [form="♀ (female)" package=THT]
  Flash = Zigbee-SmartRF-Connector [form="♀ (female)" package=THT]

nets:
  GND: PN532.GND, Buzzer.pin2, Arduino.GND, Arduino.D13~, Zigbee_Left.GND, Flash.GND
  VCC: PN532.VCC, Arduino.VIN, Zigbee_Right.VCC, Flash.VCC
  N1: PN532.SDA, Arduino.A3
  N2: PN532.SCL, Arduino.A4
  N3: Buzzer.pin1, Arduino.D6~
  N4: Arduino.TX, Zigbee_Right.P0.2
  N5: Arduino.D3~, Zigbee_Right.P0.4
  N6: Arduino.D4, Zigbee_Right.P0.6
  N7: Arduino.D5~, Zigbee_Right.P0.5
  N8: Zigbee_Left.P2.1, Flash.P2.1
  N9: Zigbee_Left.P2.2, Flash.P2.2
  N10: Zigbee_Right.RST, Flash.RST

custom parts:
  PN532 Elechouse RFID NFC Module V3: NFC is a popular technology in recent years. We often heard this work while smart phone company such as Samsung or HTC introduces their latest high-end phones. Almost all the high-end phone in the market support NFC. Near field communication (NFC) is a set of standards for smart phones and similar devices to establish radio communication with each other by touching them together or bringing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
  Arduino Nano Every: The Nano Every is Arduino’s 5V compatible board in the smallest available form factor: 45x18mm! The Arduino Nano is the preferred board for many projects requiring a small and easy to use microcontroller board. The small footprint and low price, make the Nano Every particularly suited for wearable inventions, low cost robotics, electronic musical instruments, and general use to control smaller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
  Zigbee-PA-Left: Generic double row female header
  Zigbee-PA-Right: Generic double row female header
  Zigbee-SmartRF-Connector: Generic double row female header
